# Fritzing sketch ELFATAOUY_AHARHAR (saved by Fritzing 0.9.3b)
breadboards: 1

parts:
  hc-sr1 = hc-sr04
  BT1 = Bluetooth HC-06d [package=THT]
  S1 = H-Bridge with L298N
  Composant1 = Arduino Uno (Rev3)
  J1 = Basic Servo
  M2 = DC Motor
  M5 = fc-51 [package=THT]
  M6 = fc-51 [package=THT]
  M7 = fc-51 [package=THT]
  M8 = fc-51 [package=THT]
  M9 = fc-51 [package=THT]
  M1 = DC Motor
  M3 = DC Motor
  M4 = DC Motor

nets:
  VCC: hc-sr1.VCC, BT1.VCC, Composant1.5V, J1.vcc
  N1: hc-sr1.Trig, Composant1.D2
  N2: hc-sr1.Echo, Composant1.D3_PWM
  GND: hc-sr1.GND, BT1.GND, S1.GND, Composant1.GND, J1.gnd, M9.pin2
  N3: BT1.TXD, Composant1.D0/RX
  N4: BT1.RXD, Composant1.D1/TX
  5V: S1.5V, Composant1.VIN
  N5: S1.ENA, Composant1.D6_PWM
  N6: S1.IN1, Composant1.D13/SCK
  N7: S1.IN2, Composant1.D12/MISO
  N8: S1.IN3, Composant1.D8
  N9: S1.IN4, Composant1.D7
  N10: S1.ENB, Composant1.D5_PWM
  N11: S1.M1-01, M1.pin_2
  N12: S1.M1-02, M2.pin_1
  N13: S1.M2-01, M4.pin_2
  N14: S1.M2-02, M3.pin_1
  N15: Composant1.A0, M5.pin1
  N16: Composant1.A1, M6.pin1
  N17: Composant1.A2, M7.pin1
  N18: Composant1.A3, M8.pin1
  N19: Composant1.A4/SDA, M9.pin1
  N20: Composant1.D9_PWM, J1.pulse

custom parts:
  Bluetooth HC-06d: Bluetooth HC-06 - face down, pins down 16.5mm x 37.5mm PCB
  H-Bridge with L298N: h-bridge
